# Fritzing sketch Transistor Circuit Bike Flasher (saved by Fritzing 0.9.9b)
circuit board: 4.6cm x 3cm
breadboards: 1

parts:
  Q1 = PNP-Transistor [package="TO92 [THT]"]
  R1 = Resistor [tolerance=±5% power=0.25 resistance=2k package=THT]
  C1 = Ceramic Capacitor [capacitance=47nF voltage=35V package="100 mil [THT, multilayer]"]
  R2 = Resistor [tolerance=±5% power=0.25 resistance=220 package=THT]
  R3 = Resistor [tolerance=±5% power=0.25 resistance=3M package=THT]
  Q2 = NPN-Transistor [package="TO92 [THT]"]
  VCC1 = Battery
  R4 = Resistor [tolerance=±5% power=0.25 resistance=220 package=THT]
  LED2 = LED - 5mm [color="Red (633nm)" current=0.030 package="5 mm [THT]"]
  LED1 = LED - 5mm [color="Red (633nm)" current=0.030 package="5 mm [THT]"]
  LED3 = LED - 5mm [color="Red (633nm)" current=0.030 package="5 mm [THT]"]

nets:
  N1: Q1.E, VCC1.+, R4.Pin_1, LED2.anode, LED1.anode, LED3.anode
  N2: Q1.B, R1.Pin_0, R3.Pin_0
  N3: Q1.C, R2.Pin_0
  N4: R1.Pin_1, C1.0
  N5: C1.1, Q2.C, R4.Pin_0, LED2.cathode, LED1.cathode, LED3.cathode
  N6: R2.Pin_1, Q2.B
  N7: R3.Pin_1, Q2.E, VCC1.-
