# Fritzing sketch Transistor Circuit Key Hole Light (saved by Fritzing 0.9.9b)
circuit board: 3cm x 2.7cm
breadboards: 1

parts:
  S1 = Pushbutton [package=THT]
  R1 = Resistor [tolerance=±5% power=0.25 resistance=100k package=THT]
  C1 = Ceramic Capacitor [capacitance=0.1mF voltage=35V package="100 mil [THT, multilayer]"]
  D1 = Rectifier Diode [part_number=1N4001 package="300 mil [THT]"]
  D2 = Rectifier Diode [part_number=1N4001 package="300 mil [THT]"]
  Q1 = NPN-Transistor [package="TO92 [THT]"]
  R2 = Resistor [tolerance=±5% power=0.25 resistance=220 package=THT]
  LED1 = LED - 5mm [color="Red (633nm)" current=0.030 package="5 mm [THT]"]
  VCC1 = Battery block 9V

nets:
  N1: S1.leg0, R1.Pin_0, C1.1
  N2: S1.leg1, LED1.anode, VCC1.+
  N3: R1.Pin_1, D2.anode, Q1.B
  N4: C1.0, D1.cathode, R2.Pin_0, VCC1.-
  N5: D1.anode, D2.cathode
  N6: Q1.E, R2.Pin_1
  N7: Q1.C, LED1.cathode
